# Fritzing sketch bluetooth_scrollwheel (saved by Fritzing 0.8.7b)
breadboards: 1

parts:
  TRINKET1 = Trinket 5V
  ENCODER1 = Rotary Encoder with Knob
  Adafruit_Bluefruit_HID1 = Adafruit Bluefruit Bluetooth Module
  BATT1 = 4xAA Switchable Battery Pack w/Bare Wire

nets:
  N1: TRINKET1.no_name_yet#1, Adafruit_Bluefruit_HID1.Vin, BATT1.POS
  N2: TRINKET1.no_name_yet#2, ENCODER1.no_name_yet#2, ENCODER1.no_name_yet#4, Adafruit_Bluefruit_HID1.G, BATT1.NEG
  N3: TRINKET1.no_name_yet#4, ENCODER1.no_name_yet#5
  N4: TRINKET1.no_name_yet#7, ENCODER1.no_name_yet#3
  N5: TRINKET1.no_name_yet#8, Adafruit_Bluefruit_HID1.RX
  N6: TRINKET1.no_name_yet#9, ENCODER1.no_name_yet#1
  N7: Adafruit_Bluefruit_HID1.5V, Adafruit_Bluefruit_HID1.CS
  N8: Adafruit_Bluefruit_HID1.CLK, Adafruit_Bluefruit_HID1.GND

custom parts:
  Trinket 5V: Adafruit Trinket 5V
  Rotary Encoder with Knob: Rotary Encoder with 1/4" Shaft and Knob
  4xAA Switchable Battery Pack w/Bare Wire: 4xAA Switchable Battery Pack with Bare Wire connection
